// Logisim project ROCK_PAPER_SCISSOR.circ as structural Verilog
module main (
  input  A,
  input  B,
  input  C,
  input  D,
  output C_AND_D,
  output A_AND_B
);

  wire and_1_out, and_2_out, and_3_out, and_4_out, and_5_out, and_6_out, not_1_out, not_2_out, not_3_out,
       not_4_out;

  not not_1 (not_1_out, A);
  and and_1 (and_1_out, not_1_out, not_2_out, C, D);
  not not_2 (not_2_out, B);
  not not_3 (not_3_out, C);
  and and_2 (and_2_out, A, not_2_out, not_3_out, not_4_out);
  or or_1 (A_AND_B, and_3_out, and_2_out, and_1_out);
  not not_4 (not_4_out, D);
  and and_3 (and_3_out, A, B, B, C, not_4_out);
  and and_4 (and_4_out, C, not_2_out, not_4_out, not_1_out);
  and and_5 (and_5_out, not_2_out, D, C, A);
  and and_6 (and_6_out, not_4_out, not_3_out, B, A);
  or or_2 (C_AND_D, and_4_out, and_5_out, and_6_out);

  // Notes on the sheet:
  //   AN
  //   BN
  //   CN
  //   DN
  //   K-map for RESULT OF C and D = A'B'CD' + AB'CD + ABC'D'
  //   K-map for RESULT OF A and B = A'B'CD + AB'C'D' + ABCD'
  //   an
  //   a
  //   bn
  //   b
  //   cn
  //   c
  //   d
  //   dn
endmodule

module circ100 (
  input  in_1,
  input  in_2,
  input  in_3,
  input  in_4
);

  wire main_1_a_and_b, main_1_c_and_d;

  main main_1 (.A(in_1), .B(in_2), .C(in_3), .D(in_4), .C_AND_D(main_1_c_and_d), .A_AND_B(main_1_a_and_b));
endmodule

module counter (
  input  CLOCK,
  input  INPUT_SIGNAL,
  input  ALWAYS_ZERO,
  input  RESET,
  output I3,
  output I2,
  output I1,
  output I0
);

  wire adder_1_cout, adder_1_out, adder_2_cout, adder_2_out, adder_3_cout, adder_3_out, adder_4_out,
       d_ff_1_qn;

  Adder #(.width(1)) adder_1 (.a(I3), .b(ALWAYS_ZERO), .out(adder_1_out), .cin(INPUT_SIGNAL), .cout(adder_1_cout));
  Adder #(.width(1)) adder_2 (.a(I2), .b(ALWAYS_ZERO), .out(adder_2_out), .cin(adder_1_cout), .cout(adder_2_cout));
  Adder #(.width(1)) adder_3 (.a(I1), .b(ALWAYS_ZERO), .out(adder_3_out), .cin(adder_2_cout), .cout(adder_3_cout));
  Adder #(.width(1)) adder_4 (.a(I0), .b(ALWAYS_ZERO), .out(adder_4_out), .cin(adder_3_cout));  // open: cout
  D_Flip_Flop d_ff_1 (.clk(CLOCK), .D(adder_1_out), .Q(I3), .Qn(d_ff_1_qn), .reset(RESET));  // open: preset, en
  D_Flip_Flop d_ff_2 (.clk(CLOCK), .D(adder_2_out), .Q(I2), .reset(RESET));  // open: Qn, preset, en
  D_Flip_Flop d_ff_3 (.clk(CLOCK), .D(adder_3_out), .Q(I1), .reset(RESET));  // open: Qn, preset, en
  D_Flip_Flop d_ff_4 (.clk(CLOCK), .D(adder_4_out), .Q(I0), .reset(RESET));  // open: Qn, preset, en

  // Notes on the sheet:
  //   Four adders have been used and as a register, the result of register (D-FLIP FLOP) is being feedbacked to the adders
endmodule

module \final  (
  input  EVALUATE,
  input  PLayer_1_Input_0,
  input  Player1__Input_1,
  input  Player2__Input_0,
  input  Player2__Input_1,
  input  Always_zero,
  input  RESET_SCORE
);

  wire and_1_out, and_2_out, and_3_out, clock_1_out, comparator_1_eq, comparator_1_gt, comparator_1_lt,
       main_1_a_and_b, main_1_c_and_d;
  wire [3:0] counter_1_i3, counter_2_i3;

  main main_1 (
    .A(PLayer_1_Input_0), .B(Player1__Input_1), .C(Player2__Input_0), .D(Player2__Input_1),
    .C_AND_D(main_1_c_and_d), .A_AND_B(main_1_a_and_b));
  Clock clock_1 (.out(clock_1_out));
  counter counter_1 (
    .INPUT_SIGNAL(main_1_a_and_b), .ALWAYS_ZERO(Always_zero), .RESET(RESET_SCORE), .I3(counter_1_i3[0]),
    .I2(counter_1_i3[1]), .I1(counter_1_i3[2]), .I0(counter_1_i3[3]), .CLOCK(clock_1_out));
  counter counter_2 (
    .INPUT_SIGNAL(main_1_c_and_d), .ALWAYS_ZERO(Always_zero), .RESET(RESET_SCORE), .I3(counter_2_i3[0]),
    .I2(counter_2_i3[1]), .I1(counter_2_i3[2]), .I0(counter_2_i3[3]), .CLOCK(clock_1_out));
  Hex_Digit_Display hex_digit_display_1 (.value(counter_1_i3));  // open: dp
  Hex_Digit_Display hex_digit_display_2 (.value(counter_2_i3));  // open: dp
  LED PLAYER_A_IS_WINNER (.in(and_1_out));
  LED TIE_BETWEEN_BOTH_PLAYERS (.in(and_2_out));
  and and_1 (and_1_out, EVALUATE, comparator_1_gt);
  Comparator #(.width(4), .mode("unsigned")) comparator_1 (
    .a(counter_1_i3), .b(counter_2_i3), .gt(comparator_1_gt), .eq(comparator_1_eq), .lt(comparator_1_lt));
  LED PLayer_B_won (.in(and_3_out));
  and and_2 (and_2_out, EVALUATE, comparator_1_eq);
  and and_3 (and_3_out, EVALUATE, comparator_1_lt);

  // Notes on the sheet:
  //   00 Represents ROCK
  //   10 Represents PAPER
  //   11 Represents SCISSOR
  //   Evaluate button will display who is winning based on stored results
  //   PLAYER A SCORE = 
  //   PLAYER B SCORE = 
endmodule
